# Fritzing sketch led strip (saved by Fritzing 0.9.3b)
breadboards: 1

parts:
  Part2 = Arduino Uno (Rev3) - ICSP
  IR2 = TSOP312.., 314.. [package=THT]
  NEOPIXEL1 = Neopixel Strip -- White (60/m) [part_number=1138]
  PS1 = prefix0000 [part_number=S-350-60]

nets:
  N1: Part2.D8, NEOPIXEL1.DI
  N2: Part2.D2, IR2.GND
  5V: Part2.5V, IR2.Data, NEOPIXEL1.+5V, PS1.connector2
  GND: Part2.GND, IR2.Vs, NEOPIXEL1.GND, PS1.connector4

notes:
  To the wall

custom parts:
  Neopixel Strip -- White (60/m): Neopixel Strip, White, 60 pixels per meter.
